// Logisim project increasing complexity.circ as structural Verilog
module transistor_basics (
  input  source,
  input  source_2,
  input  gate,
  input  gate_2,
  input  source_3,
  input  source_4,
  input  gate_3,
  input  gate_4,
  output drain,
  output drain_2,
  output drain_3,
  output drain_4
);

  Transistor #(.\type ("n")) transistor_1 (.in(source), .out(drain), .gate(gate));
  Transistor #(.\type ("n")) transistor_2 (.in(source_3), .out(drain_3), .gate(gate_3));
  Pull_Resistor pull_resistor_1 (.node(drain));
  Pull_Resistor pull_resistor_2 (.node(drain_3));
  Transistor transistor_3 (.in(source_2), .out(drain_2), .gate(gate_2));
  Pull_Resistor pull_resistor_3 (.node(drain_2));
  Transistor transistor_4 (.in(source_4), .out(drain_4), .gate(gate_4));
  Pull_Resistor pull_resistor_4 (.node(drain_4));

  // Notes on the sheet:
  //   n-type transistor
  //   p-type transistor
endmodule

module not__transistors (
  input  in,
  output out
);

  Transistor transistor_1 (.in(1'b1), .out(out), .gate(in));
  Transistor #(.\type ("n")) transistor_2 (.in(1'b0), .out(out), .gate(in));

  // Notes on the sheet:
  //   in: pull=down
  //   out: pull=up
  //   not gate: reverses input
endmodule

module nor__transistors (
  input  a,
  input  b,
  output out
);

  wire transistor_1_out;

  Transistor transistor_1 (.in(1'b1), .out(transistor_1_out), .gate(a));
  Transistor transistor_2 (.in(transistor_1_out), .out(out), .gate(b));
  Transistor #(.\type ("n")) transistor_3 (.in(1'b0), .out(out), .gate(a));
  Transistor #(.\type ("n")) transistor_4 (.in(1'b0), .out(out), .gate(b));
  Pull_Resistor pull_resistor_1 (.node(transistor_1_out));

  // Notes on the sheet:
  //   nor: if any input, no output
endmodule

module or__transistors (
  input  a,
  input  b,
  output out
);

  wire pull_resistor_1_node, transistor_1_out;

  Transistor #(.\type ("n")) transistor_1 (.in(1'b0), .out(transistor_1_out), .gate(b));
  Pull_Resistor pull_resistor_1 (.node(pull_resistor_1_node));
  Transistor transistor_2 (.in(1'b1), .out(pull_resistor_1_node), .gate(a));
  Transistor transistor_3 (.in(pull_resistor_1_node), .out(transistor_1_out), .gate(b));
  Transistor #(.\type ("n")) transistor_4 (.in(1'b0), .out(transistor_1_out), .gate(a));
  Transistor transistor_5 (.in(1'b1), .out(out), .gate(transistor_1_out));
  Transistor #(.\type ("n")) transistor_6 (.in(1'b0), .out(out), .gate(transistor_1_out));

  // Notes on the sheet:
  //   out: pull=up
  //   nor: if any input, no output
  //   or: if one or both inputs is active, output
  //   not gate: reverses input
endmodule

module \or  (
  input  a,
  input  b,
  output out
);

  wire nor_out;

  nor__transistors \nor  (.a(a), .b(b), .out(nor_out));
  not__transistors \not  (.in(nor_out), .out(out));

  // Notes on the sheet:
  //   or: if one or both inputs is active, output
endmodule

module nand__transistors (
  input  a,
  input  b,
  output out
);

  wire transistor_2_out, transistor_3_out;

  Transistor transistor_1 (.in(1'b1), .out(out), .gate(a));
  Transistor #(.\type ("n")) transistor_2 (.in(out), .out(transistor_2_out), .gate(a));
  Pull_Resistor pull_resistor_1 (.node(transistor_2_out));
  Transistor #(.\type ("n")) transistor_3 (.in(transistor_2_out), .out(transistor_3_out), .gate(b));
  Transistor transistor_4 (.in(1'b1), .out(out), .gate(b));
  Pull_Resistor pull_resistor_2 (.node(out));
  // also tied to GND on the sheet: transistor_3_out

  // Notes on the sheet:
  //   out: pull=up
  //   nand: does not turn off unless both inputs triggered
endmodule

module and__transistors (
  input  a,
  input  b,
  output out
);

  wire transistor_1_out, transistor_3_out, transistor_4_out;

  Transistor transistor_1 (.in(1'b1), .out(transistor_1_out), .gate(a));
  Transistor transistor_2 (.in(1'b1), .out(transistor_1_out), .gate(b));
  Transistor #(.\type ("n")) transistor_3 (.in(transistor_1_out), .out(transistor_3_out), .gate(a));
  Pull_Resistor pull_resistor_1 (.node(transistor_3_out));
  Transistor #(.\type ("n")) transistor_4 (.in(transistor_3_out), .out(transistor_4_out), .gate(b));
  Pull_Resistor pull_resistor_2 (.node(transistor_1_out));
  Transistor transistor_5 (.in(1'b1), .out(out), .gate(transistor_1_out));
  Transistor #(.\type ("n")) transistor_6 (.in(1'b0), .out(out), .gate(transistor_1_out));
  // also tied to GND on the sheet: transistor_4_out

  // Notes on the sheet:
  //   out: pull=up
  //   nand: does not turn off unless both inputs triggered
  //   and: only output if both inputs are triggered
  //   not gate: reverses input
endmodule

module \and  (
  input  a,
  input  b,
  output out
);

  wire nand_out;

  nand__transistors \nand  (.a(a), .b(b), .out(nand_out));
  not__transistors \not  (.in(nand_out), .out(out));

  // Notes on the sheet:
  //   and: only output if both inputs are triggered
endmodule
